# Fritzing sketch relay_module (saved by Fritzing 0.9.5d)

parts:
  ESP32-ETH01 = wt32-eth01
  8_Channel_Relay = 8 Channel Power Relay
  Power_5_5x2_1_5V = Power 5.5x2.5
  Switch = Taiway 100-SP-X-T1 SPDT Miniature Toggle Switch [part_number=100-SP-X-T1-0-0-B1-M2 package=THT]

nets:
  GND: ESP32-ETH01.Pin_2, ESP32-ETH01.Pin_23, 8_Channel_Relay.GND, Power_5_5x2_1_5V.GND
  N1: ESP32-ETH01.Pin_5, 8_Channel_Relay.IN8
  N2: ESP32-ETH01.Pin_6, 8_Channel_Relay.IN4
  N3: ESP32-ETH01.Pin_8, 8_Channel_Relay.IN7
  N4: ESP32-ETH01.Pin_12, 8_Channel_Relay.VCC, Switch.COM
  N5: ESP32-ETH01.Pin_15, 8_Channel_Relay.IN6
  N6: ESP32-ETH01.Pin_16, 8_Channel_Relay.IN5
  N7: ESP32-ETH01.Pin_18, 8_Channel_Relay.IN3
  N8: ESP32-ETH01.Pin_19, 8_Channel_Relay.IN2
  N9: ESP32-ETH01.Pin_20, 8_Channel_Relay.IN1
  N10: Power_5_5x2_1_5V.PWR, Switch.L1

custom parts:
  wt32-eth01: WT32-ETH01 is an embedded serial port to Ethernet module based on ESP32 series designed by Wireless-Tag.
  8 Channel Power Relay: An 8 channel power relay. The module operates at 5V.
