# Fritzing sketch remote-controller (saved by Fritzing 0.9.5d)

parts:
  Arduino_nano = Arduino Nano (Rev3.0)
  NRF24L01_+_Адаптер = NRF24L01-BO-with-pcb [package=THT]
  TP4056 = TP4056 [chip_label=TP4056 package="DIP (Dual Inline) [THT]"]
  LCD_I2C = LCD1602-I2C
  Lion_3400_mAh_3_7_V = BATTERY-2 [package=battery-aaa]
  Encoder = Encoder round
  XL6009E1 = XL6009E1 Boost Convertor
  Switch = Taiway 100-SP-X-T1 SPDT Miniature Toggle Switch [part_number=100-SP-X-T1-0-0-B1-M2 package=THT]

nets:
  GND: Arduino_nano.GND, NRF24L01_+_Адаптер.GND, TP4056.pin6, LCD_I2C.GND, Encoder.pin1, XL6009E1.Pin_2, XL6009E1.Pin_3
  N1: Arduino_nano.D2, Encoder.pin2
  N2: Arduino_nano.D3, Encoder.pin3
  N3: Arduino_nano.D4, Encoder.pin4
  N4: Arduino_nano.D9, NRF24L01_+_Адаптер.CE
  N5: Arduino_nano.D10, NRF24L01_+_Адаптер.CSN
  N6: Arduino_nano.D11/MOSI, NRF24L01_+_Адаптер.M0
  N7: Arduino_nano.D12/MISO, NRF24L01_+_Адаптер.M1
  VCC: Arduino_nano.5V, NRF24L01_+_Адаптер.VCC, LCD_I2C.VCC, Encoder.pin5, XL6009E1.Pin_4
  N8: Arduino_nano.A5, LCD_I2C.SCL
  N9: Arduino_nano.A4, LCD_I2C.SDA
  N10: Arduino_nano.D13/SCK, NRF24L01_+_Адаптер.SCK
  N11: TP4056.pin3, Switch.L1
  N12: TP4056.pin4, Lion_3400_mAh_3_7_V.+1
  N13: TP4056.pin5, Lion_3400_mAh_3_7_V.-1
  N14: XL6009E1.Pin_1, Switch.COM

custom parts:
  NRF24L01-BO-with-pcb: NRF24L01-BO breakout board for the NRF24L01. Pcb view included.
  TP4056: A DIP stand-in part for whatever IC you want. With 6 pins on a 300mil dual inline package (DIP) footprint.
  LCD1602-I2C: A standard character display, usually with 2x16 characters. Comes in many colors with LCM1602 IIC attached.
  XL6009E1 Boost Convertor: The universal DC-DC converter is made on the XL6009 chip according to the Buck-Boost Converter circuit.
